# Fritzing sketch NapkinFire (saved by Fritzing 0.9.3b)
circuit board: 6.25cm x 6.25cm
breadboards: 1

parts:
  Adafruit_ESP32 = Adafruit HUZZAH32 ESP32 Feather [part_number="Adafruit #3405"]
  LOUD = Piezo Speaker [part_number=" COM-13940"]
  PIR = PIR sensor
  J1 = double row female pin header, 16 pins [form="♀ (female)"]
  J2 = double row female pin header, 16 pins [form="♀ (female)"]
  J3 = double row female pin header, 16 pins [form="♀ (female)"]
  J4 = double row female pin header, 16 pins [form="♀ (female)"]
  ^Arducam = Arducam [package=THT]
  JMPR = Resistor [tolerance=±5% resistance=220 package="0805 [SMD]"]
  beeper = Buzzer 12mm [package=buzzer-12mm]
  microSD1 = MicroSD Breakout
  <NeoPix = Neopixel Strip -- Black (30/m)
  IR = female pin header, 6 pins [form="♀ (female)"]

nets:
  GND: Adafruit_ESP32.IO21, Adafruit_ESP32.IO17, Adafruit_ESP32.IO16, Adafruit_ESP32.GND, LOUD.pin1, PIR.GND, J1.pin1, J1.pin2, J1.pin3, J1.pin4, J1.pin5, J1.pin6, J1.pin7, J1.pin8, J1.pin9, J1.pin10, J1.pin11, J1.pin12, J1.pin13, J1.pin14, J1.pin15, J1.pin16, J2.pin1, J2.pin2, J2.pin3, J2.pin4, J2.pin5, J2.pin6, J2.pin7, J2.pin8, J2.pin9, J2.pin10, J2.pin11, J2.pin12, J2.pin13, J2.pin14, J2.pin15, J2.pin16, J3.pin1, J3.pin2, J3.pin3, J3.pin4, J3.pin5, J3.pin6, J3.pin7, J3.pin8, J3.pin9, J3.pin10, J3.pin11, J3.pin12, J3.pin13, J3.pin14, J3.pin15, J3.pin16, J4.pin1, J4.pin2, J4.pin3, J4.pin4, J4.pin5, J4.pin6, J4.pin7, J4.pin8, J4.pin9, J4.pin10, J4.pin11, J4.pin12, J4.pin13, J4.pin14, J4.pin15, J4.pin16, ^Arducam.GND, JMPR.Pin_1, beeper.1, microSD1.GND, <NeoPix.GND, IR.pin1, IR.pin2, IR.pin3
  N1: Adafruit_ESP32.MISO, ^Arducam.MISO, microSD1.DI
  N2: Adafruit_ESP32.MOSI, ^Arducam.MOSI, microSD1.DO
  N3: Adafruit_ESP32.SCK, ^Arducam.SCK, microSD1.CLK
  N4: Adafruit_ESP32.A5_IO4, <NeoPix.Din
  N5: Adafruit_ESP32.A4_IO36, IR.pin6
  N6: Adafruit_ESP32.A1_DAC1, IR.pin5
  N7: Adafruit_ESP32.A0_DAC2, IR.pin4
  3.3V: Adafruit_ESP32.3.3V, PIR.VDD, ^Arducam.VCC, JMPR.Pin_0, microSD1.3v, <NeoPix.+5V
  N8: Adafruit_ESP32.IO13_A12, microSD1.CS
  N9: Adafruit_ESP32.IO27_A10, PIR.SIG
  N10: Adafruit_ESP32.IO15_A8, beeper.2
  N11: Adafruit_ESP32.IO32_A7, LOUD.pin2
  N12: Adafruit_ESP32.IO14_A6, ^Arducam.CS
  N13: Adafruit_ESP32.SCL, ^Arducam.SCL
  N14: Adafruit_ESP32.SDA, ^Arducam.SDA

notes:
  3V
  0V
  IO1
  IO2
  IO3
  CS
  DI
  DO
  CLK
  GND
  SIG
  NeoPix

custom parts:
  Arducam: A Arducam moudle
  MicroSD Breakout: 5V-ready microSD Breakout with Level Shifter
  Neopixel Strip -- Black (30/m): These NeoPixel strips have 30 digitally-addressable pixel LEDs per meter and are very affordable and are only 12.5 mm wide, 10 mm if you remove the strip from the casing.
